# Fritzing sketch part_2 (saved by Fritzing 0.9.3b)
breadboards: 1

parts:
  부품1 = Arduino Uno (Rev3)
  J1 = Piezo Speaker
  S1 = Momentary Switch [package=ksa_sealed_tac_switch]
  R1 = Resistor [tolerance=±5% resistance=220 package="0402 [SMD]"]

nets:
  N1: 부품1.GND, J1.pin1, S1.2
  N2: 부품1.D3_PWM, S1.3
  N3: 부품1.5V, J1.pin2, R1.Pin_0
  N4: S1.4, R1.Pin_1
